// Logisim project partial-load.circ as structural Verilog: 1 circuit, main circuit partial_load
module partial_load (
  input  [31:0] Instruction,
  input  [31:0] MemAddress,
  input  [31:0] DataFromMem,
  output [31:0] DataToReg
);

  wire [7:0] multiplexer_1_out;
  wire [15:0] multiplexer_2_out;
  wire [31:0] bit_extender_1_out, bit_extender_2_out;

  Multiplexer #(.select(2), .width(8)) multiplexer_1 (
    .in0(DataFromMem[7:0]), .in1(DataFromMem[15:8]), .in2(DataFromMem[23:16]), .in3(DataFromMem[31:24]),
    .out(multiplexer_1_out), .sel(MemAddress[1:0]));
  Multiplexer #(.select(2), .width(16)) multiplexer_2 (
    .in0(DataFromMem[15:0]), .in1(DataFromMem[23:8]), .in2(DataFromMem[31:16]), .in3({16{1'b0}}),
    .out(multiplexer_2_out), .sel(MemAddress[1:0]));
  assign bit_extender_1_out = {{24{multiplexer_1_out[7]}}, multiplexer_1_out};  // Bit_Extender bit_extender_1
  assign bit_extender_2_out = {{16{multiplexer_2_out[15]}}, multiplexer_2_out};  // Bit_Extender bit_extender_2
  Multiplexer #(.select(2), .width(32)) multiplexer_3 (
    .in0(bit_extender_1_out), .in1(bit_extender_2_out), .in2(DataFromMem), .in3({32{1'b0}}), .out(DataToReg),
    .sel(Instruction[13:12]));

  // Other names for the same wires on the sheet: opcode[6:0] = Instruction[6:0]; rd[4:0] = Instruction[11:7];
  //   funct3[2:0] = Instruction[14:12]; rs1[4:0] = Instruction[19:15]; immI[11:0] = Instruction[31:20];
  //   funct7[6:0] = Instruction[31:25]

  // Notes on the sheet:
  //   INPUTS to your circuit
  //   DON'T CHANGE THE LOCATIONS OF THE INPUTS AND OUTPUTS!
  //   OUTPUT from your circuit
endmodule
