// Logisim project regfile.circ as structural Verilog: 1 circuit, main circuit regfile
module regfile (
  input  [4:0] ReadIndex1,
  input  [4:0] ReadIndex2,
  input  [4:0] WriteIndex,
  input  [31:0] WriteData,
  input  RegWEn,
  input  clk,
  output [31:0] ra,
  output [31:0] sp,
  output [31:0] t0,
  output [31:0] t1,
  output [31:0] t2,
  output [31:0] s0,
  output [31:0] s1,
  output [31:0] a0,
  output [31:0] ReadData1,
  output [31:0] ReadData2
);

  wire and_1_out, and_2_out, and_3_out, and_4_out, and_5_out, and_6_out, and_7_out, and_8_out, and_9_out,
       and_10_out, and_11_out, and_12_out, and_13_out, and_14_out, and_15_out, and_16_out, and_17_out,
       and_18_out, and_19_out, and_20_out, and_21_out, and_22_out, and_23_out, and_24_out, and_25_out,
       and_26_out, and_27_out, and_28_out, and_29_out, and_30_out, and_31_out, comparator_1_eq,
       comparator_2_eq, comparator_3_eq, comparator_4_eq, comparator_5_eq, comparator_6_eq, comparator_7_eq,
       comparator_8_eq, comparator_9_eq, comparator_10_eq, comparator_11_eq, comparator_12_eq,
       comparator_13_eq, comparator_14_eq, comparator_15_eq, comparator_16_eq, comparator_17_eq,
       comparator_18_eq, comparator_19_eq, comparator_20_eq, comparator_21_eq, comparator_22_eq,
       comparator_23_eq, comparator_24_eq, comparator_25_eq, comparator_26_eq, comparator_27_eq,
       comparator_28_eq, comparator_29_eq, comparator_30_eq, comparator_31_eq, comparator_32_eq,
       comparator_33_eq, comparator_34_eq, comparator_35_eq, comparator_36_eq, comparator_37_eq,
       comparator_38_eq, comparator_39_eq, comparator_40_eq, comparator_41_eq, comparator_42_eq,
       comparator_43_eq, comparator_44_eq, comparator_45_eq, comparator_46_eq, comparator_47_eq,
       comparator_48_eq, comparator_49_eq, comparator_50_eq, comparator_51_eq, comparator_52_eq,
       comparator_53_eq, comparator_54_eq, comparator_55_eq, comparator_56_eq, comparator_57_eq,
       comparator_58_eq, comparator_59_eq, comparator_60_eq, comparator_61_eq, comparator_62_eq,
       comparator_63_eq, comparator_64_eq, comparator_65_eq, comparator_66_eq, comparator_67_eq,
       comparator_68_eq, comparator_69_eq, comparator_70_eq, comparator_71_eq, comparator_72_eq,
       comparator_73_eq, comparator_74_eq, comparator_75_eq, comparator_76_eq, comparator_77_eq,
       comparator_78_eq, comparator_79_eq, comparator_80_eq, comparator_81_eq, comparator_82_eq,
       comparator_83_eq, comparator_84_eq, comparator_85_eq, comparator_86_eq, comparator_87_eq,
       comparator_88_eq, comparator_89_eq, comparator_90_eq, comparator_91_eq, comparator_92_eq,
       comparator_93_eq, comparator_94_eq, comparator_95_eq;
  wire [4:0] adder_1_out, adder_2_out, adder_3_out, adder_4_out, adder_5_out, adder_6_out, adder_7_out,
       adder_8_out, adder_9_out, adder_10_out, adder_11_out, adder_12_out, adder_13_out, adder_14_out,
       adder_15_out, adder_16_out, adder_17_out, adder_18_out, adder_19_out, adder_20_out, adder_21_out,
       adder_22_out, adder_23_out, adder_24_out, adder_25_out, adder_26_out, adder_27_out, adder_28_out,
       adder_29_out, adder_30_out, adder_31_out, adder_32_out, adder_33_out, adder_34_out, adder_35_out,
       adder_36_out, adder_37_out, adder_38_out, adder_39_out, adder_40_out, adder_41_out, adder_42_out,
       adder_43_out, adder_44_out, adder_45_out, adder_46_out, adder_47_out, adder_48_out, adder_49_out,
       adder_50_out, adder_51_out, adder_52_out, adder_53_out, adder_54_out, adder_55_out, adder_56_out,
       adder_57_out, adder_58_out, adder_59_out, adder_60_out, adder_61_out, adder_62_out, adder_63_out,
       adder_64_out;
  wire [31:0] multiplexer_1_out, multiplexer_2_out, multiplexer_3_out, multiplexer_4_out, multiplexer_5_out,
       multiplexer_6_out, multiplexer_7_out, multiplexer_8_out, multiplexer_9_out, multiplexer_10_out,
       multiplexer_11_out, multiplexer_12_out, multiplexer_13_out, multiplexer_14_out, multiplexer_15_out,
       multiplexer_16_out, multiplexer_17_out, multiplexer_18_out, multiplexer_19_out, multiplexer_20_out,
       multiplexer_21_out, multiplexer_22_out, multiplexer_23_out, multiplexer_24_out, multiplexer_25_out,
       multiplexer_26_out, multiplexer_27_out, multiplexer_28_out, multiplexer_29_out, multiplexer_30_out,
       multiplexer_31_out, multiplexer_32_out, multiplexer_33_out, multiplexer_34_out, multiplexer_35_out,
       multiplexer_36_out, multiplexer_37_out, multiplexer_38_out, multiplexer_39_out, multiplexer_40_out,
       multiplexer_41_out, multiplexer_42_out, multiplexer_43_out, multiplexer_44_out, multiplexer_45_out,
       multiplexer_46_out, multiplexer_47_out, multiplexer_48_out, multiplexer_49_out, multiplexer_50_out,
       multiplexer_51_out, multiplexer_52_out, multiplexer_53_out, multiplexer_54_out, multiplexer_55_out,
       multiplexer_56_out, multiplexer_57_out, multiplexer_58_out, multiplexer_59_out, multiplexer_60_out,
       multiplexer_61_out, multiplexer_62_out, multiplexer_63_out, multiplexer_64_out, or_1_out, or_2_out,
       or_4_out, or_5_out, or_7_out, or_8_out, or_9_out, or_10_out, r3, r4, r11, r12, r13, r14, r15, r16,
       r17, r18, r19, r20, r21, r22, r23, r24, r25, r26, r27, r28, r29, r30, r31;

  Comparator #(.width(5)) comparator_1 (.a(5'b00001), .b(WriteIndex), .eq(comparator_1_eq));  // open: gt, lt
  Comparator #(.width(5)) comparator_2 (.a(5'b00010), .b(WriteIndex), .eq(comparator_2_eq));  // open: gt, lt
  Comparator #(.width(5)) comparator_3 (.a(5'b00011), .b(WriteIndex), .eq(comparator_3_eq));  // open: gt, lt
  Comparator #(.width(5)) comparator_4 (.a(5'b00100), .b(WriteIndex), .eq(comparator_4_eq));  // open: gt, lt
  Comparator #(.width(5)) comparator_5 (.a(5'b00101), .b(WriteIndex), .eq(comparator_5_eq));  // open: gt, lt
  Comparator #(.width(5)) comparator_6 (.a(5'b00110), .b(WriteIndex), .eq(comparator_6_eq));  // open: gt, lt
  Comparator #(.width(5)) comparator_7 (.a(5'b00111), .b(WriteIndex), .eq(comparator_7_eq));  // open: gt, lt
  Comparator #(.width(5)) comparator_8 (.a(5'b01000), .b(WriteIndex), .eq(comparator_8_eq));  // open: gt, lt
  Register #(.width(32)) register_1 (.D(WriteData), .en(and_1_out), .clk(clk), .Q(ra));  // open: clr
  and and_1 (and_1_out, comparator_1_eq, RegWEn);
  Register #(.width(32)) register_2 (.D(WriteData), .en(and_2_out), .clk(clk), .Q(sp));  // open: clr
  and and_2 (and_2_out, comparator_2_eq, RegWEn);
  Register #(.width(32)) register_3 (.D(WriteData), .en(and_3_out), .clk(clk), .Q(r3));  // open: clr
  and and_3 (and_3_out, comparator_3_eq, RegWEn);
  Register #(.width(32)) register_4 (.D(WriteData), .en(and_4_out), .clk(clk), .Q(r4));  // open: clr
  and and_4 (and_4_out, comparator_4_eq, RegWEn);
  Register #(.width(32)) register_5 (.D(WriteData), .en(and_5_out), .clk(clk), .Q(t0));  // open: clr
  and and_5 (and_5_out, comparator_5_eq, RegWEn);
  Register #(.width(32)) register_6 (.D(WriteData), .en(and_6_out), .clk(clk), .Q(t1));  // open: clr
  and and_6 (and_6_out, comparator_6_eq, RegWEn);
  Register #(.width(32)) register_7 (.D(WriteData), .en(and_7_out), .clk(clk), .Q(t2));  // open: clr
  and and_7 (and_7_out, comparator_7_eq, RegWEn);
  Register #(.width(32)) register_8 (.D(WriteData), .en(and_8_out), .clk(clk), .Q(s0));  // open: clr
  and and_8 (and_8_out, comparator_8_eq, RegWEn);
  Comparator #(.width(5)) comparator_9 (.a(5'b01001), .b(WriteIndex), .eq(comparator_9_eq));  // open: gt, lt
  Comparator #(.width(5)) comparator_10 (.a(5'b01010), .b(WriteIndex), .eq(comparator_10_eq));  // open: gt, lt
  Comparator #(.width(5)) comparator_11 (.a(5'b01011), .b(WriteIndex), .eq(comparator_11_eq));  // open: gt, lt
  Comparator #(.width(5)) comparator_12 (.a(5'b01100), .b(WriteIndex), .eq(comparator_12_eq));  // open: gt, lt
  Comparator #(.width(5)) comparator_13 (.a(5'b01101), .b(WriteIndex), .eq(comparator_13_eq));  // open: gt, lt
  Comparator #(.width(5)) comparator_14 (.a(5'b01110), .b(WriteIndex), .eq(comparator_14_eq));  // open: gt, lt
  Comparator #(.width(5)) comparator_15 (.a(5'b01111), .b(WriteIndex), .eq(comparator_15_eq));  // open: gt, lt
  Comparator #(.width(5)) comparator_16 (.a(5'b10000), .b(WriteIndex), .eq(comparator_16_eq));  // open: gt, lt
  Register #(.width(32)) register_9 (.D(WriteData), .en(and_9_out), .clk(clk), .Q(s1));  // open: clr
  and and_9 (and_9_out, comparator_9_eq, RegWEn);
  Register #(.width(32)) register_10 (.D(WriteData), .en(and_10_out), .clk(clk), .Q(a0));  // open: clr
  and and_10 (and_10_out, comparator_10_eq, RegWEn);
  Register #(.width(32)) register_11 (.D(WriteData), .en(and_11_out), .clk(clk), .Q(r11));  // open: clr
  and and_11 (and_11_out, comparator_11_eq, RegWEn);
  Register #(.width(32)) register_12 (.D(WriteData), .en(and_12_out), .clk(clk), .Q(r12));  // open: clr
  and and_12 (and_12_out, comparator_12_eq, RegWEn);
  Register #(.width(32)) register_13 (.D(WriteData), .en(and_13_out), .clk(clk), .Q(r13));  // open: clr
  and and_13 (and_13_out, comparator_13_eq, RegWEn);
  Register #(.width(32)) register_14 (.D(WriteData), .en(and_14_out), .clk(clk), .Q(r14));  // open: clr
  and and_14 (and_14_out, comparator_14_eq, RegWEn);
  Register #(.width(32)) register_15 (.D(WriteData), .en(and_15_out), .clk(clk), .Q(r15));  // open: clr
  and and_15 (and_15_out, comparator_15_eq, RegWEn);
  Register #(.width(32)) register_16 (.D(WriteData), .en(and_16_out), .clk(clk), .Q(r16));  // open: clr
  and and_16 (and_16_out, comparator_16_eq, RegWEn);
  Comparator #(.width(5)) comparator_17 (.a(5'b10001), .b(WriteIndex), .eq(comparator_17_eq));  // open: gt, lt
  Comparator #(.width(5)) comparator_18 (.a(5'b10010), .b(WriteIndex), .eq(comparator_18_eq));  // open: gt, lt
  Comparator #(.width(5)) comparator_19 (.a(5'b10011), .b(WriteIndex), .eq(comparator_19_eq));  // open: gt, lt
  Comparator #(.width(5)) comparator_20 (.a(5'b10100), .b(WriteIndex), .eq(comparator_20_eq));  // open: gt, lt
  Comparator #(.width(5)) comparator_21 (.a(5'b10101), .b(WriteIndex), .eq(comparator_21_eq));  // open: gt, lt
  Comparator #(.width(5)) comparator_22 (.a(5'b10110), .b(WriteIndex), .eq(comparator_22_eq));  // open: gt, lt
  Comparator #(.width(5)) comparator_23 (.a(5'b10111), .b(WriteIndex), .eq(comparator_23_eq));  // open: gt, lt
  Comparator #(.width(5)) comparator_24 (.a(5'b11000), .b(WriteIndex), .eq(comparator_24_eq));  // open: gt, lt
  and and_17 (and_17_out, comparator_17_eq, RegWEn);
  and and_18 (and_18_out, comparator_18_eq, RegWEn);
  and and_19 (and_19_out, comparator_19_eq, RegWEn);
  and and_20 (and_20_out, comparator_20_eq, RegWEn);
  Register #(.width(32)) register_17 (.D(WriteData), .en(and_17_out), .clk(clk), .Q(r17));  // open: clr
  Register #(.width(32)) register_18 (.D(WriteData), .en(and_18_out), .clk(clk), .Q(r18));  // open: clr
  Register #(.width(32)) register_19 (.D(WriteData), .en(and_19_out), .clk(clk), .Q(r19));  // open: clr
  Register #(.width(32)) register_20 (.D(WriteData), .en(and_20_out), .clk(clk), .Q(r20));  // open: clr
  Register #(.width(32)) register_21 (.D(WriteData), .en(and_21_out), .clk(clk), .Q(r21));  // open: clr
  and and_21 (and_21_out, comparator_21_eq, RegWEn);
  Register #(.width(32)) register_22 (.D(WriteData), .en(and_22_out), .clk(clk), .Q(r22));  // open: clr
  and and_22 (and_22_out, comparator_22_eq, RegWEn);
  Register #(.width(32)) register_23 (.D(WriteData), .en(and_23_out), .clk(clk), .Q(r23));  // open: clr
  and and_23 (and_23_out, comparator_23_eq, RegWEn);
  Register #(.width(32)) register_24 (.D(WriteData), .en(and_24_out), .clk(clk), .Q(r24));  // open: clr
  and and_24 (and_24_out, comparator_24_eq, RegWEn);
  Comparator #(.width(5)) comparator_25 (.a(5'b11001), .b(WriteIndex), .eq(comparator_25_eq));  // open: gt, lt
  Comparator #(.width(5)) comparator_26 (.a(5'b11010), .b(WriteIndex), .eq(comparator_26_eq));  // open: gt, lt
  Comparator #(.width(5)) comparator_27 (.a(5'b11011), .b(WriteIndex), .eq(comparator_27_eq));  // open: gt, lt
  Comparator #(.width(5)) comparator_28 (.a(5'b11100), .b(WriteIndex), .eq(comparator_28_eq));  // open: gt, lt
  Comparator #(.width(5)) comparator_29 (.a(5'b11101), .b(WriteIndex), .eq(comparator_29_eq));  // open: gt, lt
  Comparator #(.width(5)) comparator_30 (.a(5'b11110), .b(WriteIndex), .eq(comparator_30_eq));  // open: gt, lt
  Comparator #(.width(5)) comparator_31 (.a({5{1'b1}}), .b(WriteIndex), .eq(comparator_31_eq));  // open: gt, lt
  and and_25 (and_25_out, comparator_25_eq, RegWEn);
  and and_26 (and_26_out, comparator_26_eq, RegWEn);
  and and_27 (and_27_out, comparator_27_eq, RegWEn);
  and and_28 (and_28_out, comparator_28_eq, RegWEn);
  and and_29 (and_29_out, comparator_29_eq, RegWEn);
  and and_30 (and_30_out, comparator_30_eq, RegWEn);
  and and_31 (and_31_out, comparator_31_eq, RegWEn);
  Register #(.width(32)) register_25 (.D(WriteData), .en(and_25_out), .clk(clk), .Q(r25));  // open: clr
  Register #(.width(32)) register_26 (.D(WriteData), .en(and_26_out), .clk(clk), .Q(r26));  // open: clr
  Register #(.width(32)) register_27 (.D(WriteData), .en(and_27_out), .clk(clk), .Q(r27));  // open: clr
  Register #(.width(32)) register_28 (.D(WriteData), .en(and_28_out), .clk(clk), .Q(r28));  // open: clr
  Register #(.width(32)) register_29 (.D(WriteData), .en(and_29_out), .clk(clk), .Q(r29));  // open: clr
  Register #(.width(32)) register_30 (.D(WriteData), .en(and_30_out), .clk(clk), .Q(r30));  // open: clr
  Register #(.width(32)) register_31 (.D(WriteData), .en(and_31_out), .clk(clk), .Q(r31));  // open: clr
  Adder #(.width(5)) adder_1 (.a({5{1'b0}}), .b({5{1'b0}}), .out(adder_1_out));  // open: cin, cout
  Adder #(.width(5)) adder_2 (.a(5'b00001), .b({5{1'b0}}), .out(adder_2_out));  // open: cin, cout
  Adder #(.width(5)) adder_3 (.a(5'b00010), .b({5{1'b0}}), .out(adder_3_out));  // open: cin, cout
  Adder #(.width(5)) adder_4 (.a(5'b00011), .b({5{1'b0}}), .out(adder_4_out));  // open: cin, cout
  Adder #(.width(5)) adder_5 (.a(5'b00100), .b({5{1'b0}}), .out(adder_5_out));  // open: cin, cout
  Adder #(.width(5)) adder_6 (.a(5'b00101), .b({5{1'b0}}), .out(adder_6_out));  // open: cin, cout
  Adder #(.width(5)) adder_7 (.a(5'b00110), .b({5{1'b0}}), .out(adder_7_out));  // open: cin, cout
  Adder #(.width(5)) adder_8 (.a(5'b00111), .b({5{1'b0}}), .out(adder_8_out));  // open: cin, cout
  Adder #(.width(5)) adder_9 (.a({5{1'b0}}), .b({5{1'b0}}), .out(adder_9_out));  // open: cin, cout
  Adder #(.width(5)) adder_10 (.a(5'b00001), .b({5{1'b0}}), .out(adder_10_out));  // open: cin, cout
  Adder #(.width(5)) adder_11 (.a(5'b00010), .b({5{1'b0}}), .out(adder_11_out));  // open: cin, cout
  Adder #(.width(5)) adder_12 (.a(5'b00011), .b({5{1'b0}}), .out(adder_12_out));  // open: cin, cout
  Adder #(.width(5)) adder_13 (.a(5'b00100), .b({5{1'b0}}), .out(adder_13_out));  // open: cin, cout
  Adder #(.width(5)) adder_14 (.a(5'b00101), .b({5{1'b0}}), .out(adder_14_out));  // open: cin, cout
  Adder #(.width(5)) adder_15 (.a(5'b00110), .b({5{1'b0}}), .out(adder_15_out));  // open: cin, cout
  Adder #(.width(5)) adder_16 (.a(5'b00111), .b({5{1'b0}}), .out(adder_16_out));  // open: cin, cout
  Multiplexer #(.width(32)) multiplexer_1 (
    .in0({32{1'b0}}), .in1({32{1'b0}}), .out(multiplexer_1_out), .sel(comparator_32_eq));
  Comparator #(.width(5)) comparator_32 (.a(ReadIndex1), .b(adder_1_out), .eq(comparator_32_eq));  // open: gt, lt
  Multiplexer #(.width(32)) multiplexer_2 (.in0({32{1'b0}}), .in1(ra), .out(multiplexer_2_out), .sel(comparator_33_eq));
  Comparator #(.width(5)) comparator_33 (.a(ReadIndex1), .b(adder_2_out), .eq(comparator_33_eq));  // open: gt, lt
  Multiplexer #(.width(32)) multiplexer_3 (.in0({32{1'b0}}), .in1(sp), .out(multiplexer_3_out), .sel(comparator_34_eq));
  Comparator #(.width(5)) comparator_34 (.a(ReadIndex1), .b(adder_3_out), .eq(comparator_34_eq));  // open: gt, lt
  Multiplexer #(.width(32)) multiplexer_4 (.in0({32{1'b0}}), .in1(r3), .out(multiplexer_4_out), .sel(comparator_35_eq));
  Comparator #(.width(5)) comparator_35 (.a(ReadIndex1), .b(adder_4_out), .eq(comparator_35_eq));  // open: gt, lt
  Multiplexer #(.width(32)) multiplexer_5 (.in0({32{1'b0}}), .in1(r4), .out(multiplexer_5_out), .sel(comparator_36_eq));
  Comparator #(.width(5)) comparator_36 (.a(ReadIndex1), .b(adder_5_out), .eq(comparator_36_eq));  // open: gt, lt
  Multiplexer #(.width(32)) multiplexer_6 (.in0({32{1'b0}}), .in1(t0), .out(multiplexer_6_out), .sel(comparator_37_eq));
  Comparator #(.width(5)) comparator_37 (.a(ReadIndex1), .b(adder_6_out), .eq(comparator_37_eq));  // open: gt, lt
  Multiplexer #(.width(32)) multiplexer_7 (.in0({32{1'b0}}), .in1(t1), .out(multiplexer_7_out), .sel(comparator_38_eq));
  Comparator #(.width(5)) comparator_38 (.a(ReadIndex1), .b(adder_7_out), .eq(comparator_38_eq));  // open: gt, lt
  Multiplexer #(.width(32)) multiplexer_8 (.in0({32{1'b0}}), .in1(t2), .out(multiplexer_8_out), .sel(comparator_39_eq));
  Comparator #(.width(5)) comparator_39 (.a(ReadIndex1), .b(adder_8_out), .eq(comparator_39_eq));  // open: gt, lt
  Comparator #(.width(5)) comparator_40 (.a(ReadIndex2), .b(adder_9_out), .eq(comparator_40_eq));  // open: gt, lt
  Comparator #(.width(5)) comparator_41 (.a(ReadIndex2), .b(adder_10_out), .eq(comparator_41_eq));  // open: gt, lt
  Comparator #(.width(5)) comparator_42 (.a(ReadIndex2), .b(adder_11_out), .eq(comparator_42_eq));  // open: gt, lt
  Comparator #(.width(5)) comparator_43 (.a(ReadIndex2), .b(adder_12_out), .eq(comparator_43_eq));  // open: gt, lt
  Comparator #(.width(5)) comparator_44 (.a(ReadIndex2), .b(adder_13_out), .eq(comparator_44_eq));  // open: gt, lt
  Comparator #(.width(5)) comparator_45 (.a(ReadIndex2), .b(adder_14_out), .eq(comparator_45_eq));  // open: gt, lt
  Comparator #(.width(5)) comparator_46 (.a(ReadIndex2), .b(adder_15_out), .eq(comparator_46_eq));  // open: gt, lt
  Comparator #(.width(5)) comparator_47 (.a(ReadIndex2), .b(adder_16_out), .eq(comparator_47_eq));  // open: gt, lt
  Multiplexer #(.width(32)) multiplexer_9 (
    .in0({32{1'b0}}), .in1({32{1'b0}}), .out(multiplexer_9_out), .sel(comparator_40_eq));
  Multiplexer #(.width(32)) multiplexer_10 (
    .in0({32{1'b0}}), .in1(ra), .out(multiplexer_10_out), .sel(comparator_41_eq));
  Multiplexer #(.width(32)) multiplexer_11 (
    .in0({32{1'b0}}), .in1(sp), .out(multiplexer_11_out), .sel(comparator_42_eq));
  Multiplexer #(.width(32)) multiplexer_12 (
    .in0({32{1'b0}}), .in1(r3), .out(multiplexer_12_out), .sel(comparator_43_eq));
  Multiplexer #(.width(32)) multiplexer_13 (
    .in0({32{1'b0}}), .in1(r4), .out(multiplexer_13_out), .sel(comparator_44_eq));
  Multiplexer #(.width(32)) multiplexer_14 (
    .in0({32{1'b0}}), .in1(t0), .out(multiplexer_14_out), .sel(comparator_45_eq));
  Multiplexer #(.width(32)) multiplexer_15 (
    .in0({32{1'b0}}), .in1(t1), .out(multiplexer_15_out), .sel(comparator_46_eq));
  Multiplexer #(.width(32)) multiplexer_16 (
    .in0({32{1'b0}}), .in1(t2), .out(multiplexer_16_out), .sel(comparator_47_eq));
  assign or_1_out = multiplexer_1_out | multiplexer_2_out | multiplexer_3_out | multiplexer_4_out | multiplexer_5_out | multiplexer_6_out | multiplexer_7_out | multiplexer_8_out;  // OR_Gate or_1, 32 bits wide
  assign or_2_out = multiplexer_9_out | multiplexer_10_out | multiplexer_11_out | multiplexer_12_out | multiplexer_13_out | multiplexer_14_out | multiplexer_15_out | multiplexer_16_out;  // OR_Gate or_2, 32 bits wide
  Adder #(.width(5)) adder_17 (.a({5{1'b0}}), .b(5'b01000), .out(adder_17_out));  // open: cin, cout
  Adder #(.width(5)) adder_18 (.a(5'b00001), .b(5'b01000), .out(adder_18_out));  // open: cin, cout
  Adder #(.width(5)) adder_19 (.a(5'b00010), .b(5'b01000), .out(adder_19_out));  // open: cin, cout
  Adder #(.width(5)) adder_20 (.a(5'b00011), .b(5'b01000), .out(adder_20_out));  // open: cin, cout
  Adder #(.width(5)) adder_21 (.a(5'b00100), .b(5'b01000), .out(adder_21_out));  // open: cin, cout
  Adder #(.width(5)) adder_22 (.a(5'b00101), .b(5'b01000), .out(adder_22_out));  // open: cin, cout
  Adder #(.width(5)) adder_23 (.a(5'b00110), .b(5'b01000), .out(adder_23_out));  // open: cin, cout
  Adder #(.width(5)) adder_24 (.a(5'b00111), .b(5'b01000), .out(adder_24_out));  // open: cin, cout
  Adder #(.width(5)) adder_25 (.a({5{1'b0}}), .b(5'b01000), .out(adder_25_out));  // open: cin, cout
  Adder #(.width(5)) adder_26 (.a(5'b00001), .b(5'b01000), .out(adder_26_out));  // open: cin, cout
  Adder #(.width(5)) adder_27 (.a(5'b00010), .b(5'b01000), .out(adder_27_out));  // open: cin, cout
  Adder #(.width(5)) adder_28 (.a(5'b00011), .b(5'b01000), .out(adder_28_out));  // open: cin, cout
  Adder #(.width(5)) adder_29 (.a(5'b00100), .b(5'b01000), .out(adder_29_out));  // open: cin, cout
  Adder #(.width(5)) adder_30 (.a(5'b00101), .b(5'b01000), .out(adder_30_out));  // open: cin, cout
  Adder #(.width(5)) adder_31 (.a(5'b00110), .b(5'b01000), .out(adder_31_out));  // open: cin, cout
  Adder #(.width(5)) adder_32 (.a(5'b00111), .b(5'b01000), .out(adder_32_out));  // open: cin, cout
  Multiplexer #(.width(32)) multiplexer_17 (
    .in0({32{1'b0}}), .in1(s0), .out(multiplexer_17_out), .sel(comparator_48_eq));
  Comparator #(.width(5)) comparator_48 (.a(ReadIndex1), .b(adder_17_out), .eq(comparator_48_eq));  // open: gt, lt
  Multiplexer #(.width(32)) multiplexer_18 (
    .in0({32{1'b0}}), .in1(s1), .out(multiplexer_18_out), .sel(comparator_49_eq));
  Comparator #(.width(5)) comparator_49 (.a(ReadIndex1), .b(adder_18_out), .eq(comparator_49_eq));  // open: gt, lt
  Multiplexer #(.width(32)) multiplexer_19 (
    .in0({32{1'b0}}), .in1(a0), .out(multiplexer_19_out), .sel(comparator_50_eq));
  Comparator #(.width(5)) comparator_50 (.a(ReadIndex1), .b(adder_19_out), .eq(comparator_50_eq));  // open: gt, lt
  Multiplexer #(.width(32)) multiplexer_20 (
    .in0({32{1'b0}}), .in1(r11), .out(multiplexer_20_out), .sel(comparator_51_eq));
  Comparator #(.width(5)) comparator_51 (.a(ReadIndex1), .b(adder_20_out), .eq(comparator_51_eq));  // open: gt, lt
  Multiplexer #(.width(32)) multiplexer_21 (
    .in0({32{1'b0}}), .in1(r12), .out(multiplexer_21_out), .sel(comparator_52_eq));
  Comparator #(.width(5)) comparator_52 (.a(ReadIndex1), .b(adder_21_out), .eq(comparator_52_eq));  // open: gt, lt
  Multiplexer #(.width(32)) multiplexer_22 (
    .in0({32{1'b0}}), .in1(r13), .out(multiplexer_22_out), .sel(comparator_53_eq));
  Comparator #(.width(5)) comparator_53 (.a(ReadIndex1), .b(adder_22_out), .eq(comparator_53_eq));  // open: gt, lt
  Multiplexer #(.width(32)) multiplexer_23 (
    .in0({32{1'b0}}), .in1(r14), .out(multiplexer_23_out), .sel(comparator_54_eq));
  Comparator #(.width(5)) comparator_54 (.a(ReadIndex1), .b(adder_23_out), .eq(comparator_54_eq));  // open: gt, lt
  Multiplexer #(.width(32)) multiplexer_24 (
    .in0({32{1'b0}}), .in1(r15), .out(multiplexer_24_out), .sel(comparator_55_eq));
  Comparator #(.width(5)) comparator_55 (.a(ReadIndex1), .b(adder_24_out), .eq(comparator_55_eq));  // open: gt, lt
  Comparator #(.width(5)) comparator_56 (.a(ReadIndex2), .b(adder_25_out), .eq(comparator_56_eq));  // open: gt, lt
  Comparator #(.width(5)) comparator_57 (.a(ReadIndex2), .b(adder_26_out), .eq(comparator_57_eq));  // open: gt, lt
  Comparator #(.width(5)) comparator_58 (.a(ReadIndex2), .b(adder_27_out), .eq(comparator_58_eq));  // open: gt, lt
  Comparator #(.width(5)) comparator_59 (.a(ReadIndex2), .b(adder_28_out), .eq(comparator_59_eq));  // open: gt, lt
  Comparator #(.width(5)) comparator_60 (.a(ReadIndex2), .b(adder_29_out), .eq(comparator_60_eq));  // open: gt, lt
  Comparator #(.width(5)) comparator_61 (.a(ReadIndex2), .b(adder_30_out), .eq(comparator_61_eq));  // open: gt, lt
  Comparator #(.width(5)) comparator_62 (.a(ReadIndex2), .b(adder_31_out), .eq(comparator_62_eq));  // open: gt, lt
  Comparator #(.width(5)) comparator_63 (.a(ReadIndex2), .b(adder_32_out), .eq(comparator_63_eq));  // open: gt, lt
  Multiplexer #(.width(32)) multiplexer_25 (
    .in0({32{1'b0}}), .in1(s0), .out(multiplexer_25_out), .sel(comparator_56_eq));
  Multiplexer #(.width(32)) multiplexer_26 (
    .in0({32{1'b0}}), .in1(s1), .out(multiplexer_26_out), .sel(comparator_57_eq));
  Multiplexer #(.width(32)) multiplexer_27 (
    .in0({32{1'b0}}), .in1(a0), .out(multiplexer_27_out), .sel(comparator_58_eq));
  Multiplexer #(.width(32)) multiplexer_28 (
    .in0({32{1'b0}}), .in1(r11), .out(multiplexer_28_out), .sel(comparator_59_eq));
  Multiplexer #(.width(32)) multiplexer_29 (
    .in0({32{1'b0}}), .in1(r12), .out(multiplexer_29_out), .sel(comparator_60_eq));
  Multiplexer #(.width(32)) multiplexer_30 (
    .in0({32{1'b0}}), .in1(r13), .out(multiplexer_30_out), .sel(comparator_61_eq));
  Multiplexer #(.width(32)) multiplexer_31 (
    .in0({32{1'b0}}), .in1(r14), .out(multiplexer_31_out), .sel(comparator_62_eq));
  Multiplexer #(.width(32)) multiplexer_32 (
    .in0({32{1'b0}}), .in1(r15), .out(multiplexer_32_out), .sel(comparator_63_eq));
  assign ReadData1 = or_1_out | or_4_out | or_7_out | or_9_out;  // OR_Gate or_3, 32 bits wide
  assign or_4_out = multiplexer_17_out | multiplexer_18_out | multiplexer_19_out | multiplexer_20_out | multiplexer_21_out | multiplexer_22_out | multiplexer_23_out | multiplexer_24_out;  // OR_Gate or_4, 32 bits wide
  assign or_5_out = multiplexer_25_out | multiplexer_26_out | multiplexer_27_out | multiplexer_28_out | multiplexer_29_out | multiplexer_30_out | multiplexer_31_out | multiplexer_32_out;  // OR_Gate or_5, 32 bits wide
  assign ReadData2 = or_2_out | or_5_out | or_8_out | or_10_out;  // OR_Gate or_6, 32 bits wide
  Adder #(.width(5)) adder_33 (.a({5{1'b0}}), .b(5'b01100), .out(adder_33_out));  // open: cin, cout
  Adder #(.width(5)) adder_34 (.a(5'b00001), .b(5'b01100), .out(adder_34_out));  // open: cin, cout
  Adder #(.width(5)) adder_35 (.a(5'b00010), .b(5'b01100), .out(adder_35_out));  // open: cin, cout
  Adder #(.width(5)) adder_36 (.a(5'b00011), .b(5'b01100), .out(adder_36_out));  // open: cin, cout
  Adder #(.width(5)) adder_37 (.a(5'b00100), .b(5'b01100), .out(adder_37_out));  // open: cin, cout
  Adder #(.width(5)) adder_38 (.a(5'b00101), .b(5'b01100), .out(adder_38_out));  // open: cin, cout
  Adder #(.width(5)) adder_39 (.a(5'b00110), .b(5'b01100), .out(adder_39_out));  // open: cin, cout
  Adder #(.width(5)) adder_40 (.a(5'b00111), .b(5'b01100), .out(adder_40_out));  // open: cin, cout
  Adder #(.width(5)) adder_41 (.a({5{1'b0}}), .b(5'b01100), .out(adder_41_out));  // open: cin, cout
  Adder #(.width(5)) adder_42 (.a(5'b00001), .b(5'b01100), .out(adder_42_out));  // open: cin, cout
  Adder #(.width(5)) adder_43 (.a(5'b00010), .b(5'b01100), .out(adder_43_out));  // open: cin, cout
  Adder #(.width(5)) adder_44 (.a(5'b00011), .b(5'b01100), .out(adder_44_out));  // open: cin, cout
  Adder #(.width(5)) adder_45 (.a(5'b00100), .b(5'b01100), .out(adder_45_out));  // open: cin, cout
  Adder #(.width(5)) adder_46 (.a(5'b00101), .b(5'b01100), .out(adder_46_out));  // open: cin, cout
  Adder #(.width(5)) adder_47 (.a(5'b00110), .b(5'b01100), .out(adder_47_out));  // open: cin, cout
  Adder #(.width(5)) adder_48 (.a(5'b00111), .b(5'b01100), .out(adder_48_out));  // open: cin, cout
  Multiplexer #(.width(32)) multiplexer_33 (
    .in0({32{1'b0}}), .in1(r16), .out(multiplexer_33_out), .sel(comparator_64_eq));
  Comparator #(.width(5)) comparator_64 (.a(ReadIndex1), .b(adder_33_out), .eq(comparator_64_eq));  // open: gt, lt
  Multiplexer #(.width(32)) multiplexer_34 (
    .in0({32{1'b0}}), .in1(r17), .out(multiplexer_34_out), .sel(comparator_65_eq));
  Comparator #(.width(5)) comparator_65 (.a(ReadIndex1), .b(adder_34_out), .eq(comparator_65_eq));  // open: gt, lt
  Multiplexer #(.width(32)) multiplexer_35 (
    .in0({32{1'b0}}), .in1(r18), .out(multiplexer_35_out), .sel(comparator_66_eq));
  Comparator #(.width(5)) comparator_66 (.a(ReadIndex1), .b(adder_35_out), .eq(comparator_66_eq));  // open: gt, lt
  Multiplexer #(.width(32)) multiplexer_36 (
    .in0({32{1'b0}}), .in1(r19), .out(multiplexer_36_out), .sel(comparator_67_eq));
  Comparator #(.width(5)) comparator_67 (.a(ReadIndex1), .b(adder_36_out), .eq(comparator_67_eq));  // open: gt, lt
  Multiplexer #(.width(32)) multiplexer_37 (
    .in0({32{1'b0}}), .in1(r20), .out(multiplexer_37_out), .sel(comparator_68_eq));
  Comparator #(.width(5)) comparator_68 (.a(ReadIndex1), .b(adder_37_out), .eq(comparator_68_eq));  // open: gt, lt
  Multiplexer #(.width(32)) multiplexer_38 (
    .in0({32{1'b0}}), .in1(r21), .out(multiplexer_38_out), .sel(comparator_69_eq));
  Comparator #(.width(5)) comparator_69 (.a(ReadIndex1), .b(adder_38_out), .eq(comparator_69_eq));  // open: gt, lt
  Multiplexer #(.width(32)) multiplexer_39 (
    .in0({32{1'b0}}), .in1(r22), .out(multiplexer_39_out), .sel(comparator_70_eq));
  Comparator #(.width(5)) comparator_70 (.a(ReadIndex1), .b(adder_39_out), .eq(comparator_70_eq));  // open: gt, lt
  Multiplexer #(.width(32)) multiplexer_40 (
    .in0({32{1'b0}}), .in1(r23), .out(multiplexer_40_out), .sel(comparator_71_eq));
  Comparator #(.width(5)) comparator_71 (.a(ReadIndex1), .b(adder_40_out), .eq(comparator_71_eq));  // open: gt, lt
  Comparator #(.width(5)) comparator_72 (.a(ReadIndex2), .b(adder_41_out), .eq(comparator_72_eq));  // open: gt, lt
  Comparator #(.width(5)) comparator_73 (.a(ReadIndex2), .b(adder_42_out), .eq(comparator_73_eq));  // open: gt, lt
  Comparator #(.width(5)) comparator_74 (.a(ReadIndex2), .b(adder_43_out), .eq(comparator_74_eq));  // open: gt, lt
  Comparator #(.width(5)) comparator_75 (.a(ReadIndex2), .b(adder_44_out), .eq(comparator_75_eq));  // open: gt, lt
  Comparator #(.width(5)) comparator_76 (.a(ReadIndex2), .b(adder_45_out), .eq(comparator_76_eq));  // open: gt, lt
  Comparator #(.width(5)) comparator_77 (.a(ReadIndex2), .b(adder_46_out), .eq(comparator_77_eq));  // open: gt, lt
  Comparator #(.width(5)) comparator_78 (.a(ReadIndex2), .b(adder_47_out), .eq(comparator_78_eq));  // open: gt, lt
  Comparator #(.width(5)) comparator_79 (.a(ReadIndex2), .b(adder_48_out), .eq(comparator_79_eq));  // open: gt, lt
  Multiplexer #(.width(32)) multiplexer_41 (
    .in0({32{1'b0}}), .in1(r16), .out(multiplexer_41_out), .sel(comparator_72_eq));
  Multiplexer #(.width(32)) multiplexer_42 (
    .in0({32{1'b0}}), .in1(r17), .out(multiplexer_42_out), .sel(comparator_73_eq));
  Multiplexer #(.width(32)) multiplexer_43 (
    .in0({32{1'b0}}), .in1(r18), .out(multiplexer_43_out), .sel(comparator_74_eq));
  Multiplexer #(.width(32)) multiplexer_44 (
    .in0({32{1'b0}}), .in1(r19), .out(multiplexer_44_out), .sel(comparator_75_eq));
  Multiplexer #(.width(32)) multiplexer_45 (
    .in0({32{1'b0}}), .in1(r20), .out(multiplexer_45_out), .sel(comparator_76_eq));
  Multiplexer #(.width(32)) multiplexer_46 (
    .in0({32{1'b0}}), .in1(r21), .out(multiplexer_46_out), .sel(comparator_77_eq));
  Multiplexer #(.width(32)) multiplexer_47 (
    .in0({32{1'b0}}), .in1(r22), .out(multiplexer_47_out), .sel(comparator_78_eq));
  Multiplexer #(.width(32)) multiplexer_48 (
    .in0({32{1'b0}}), .in1(r23), .out(multiplexer_48_out), .sel(comparator_79_eq));
  assign or_7_out = multiplexer_33_out | multiplexer_34_out | multiplexer_35_out | multiplexer_36_out | multiplexer_37_out | multiplexer_38_out | multiplexer_39_out | multiplexer_40_out;  // OR_Gate or_7, 32 bits wide
  assign or_8_out = multiplexer_41_out | multiplexer_42_out | multiplexer_43_out | multiplexer_44_out | multiplexer_45_out | multiplexer_46_out | multiplexer_47_out | multiplexer_48_out;  // OR_Gate or_8, 32 bits wide
  Adder #(.width(5)) adder_49 (.a({5{1'b0}}), .b(5'b11000), .out(adder_49_out));  // open: cin, cout
  Adder #(.width(5)) adder_50 (.a(5'b00001), .b(5'b11000), .out(adder_50_out));  // open: cin, cout
  Adder #(.width(5)) adder_51 (.a(5'b00010), .b(5'b11000), .out(adder_51_out));  // open: cin, cout
  Adder #(.width(5)) adder_52 (.a(5'b00011), .b(5'b11000), .out(adder_52_out));  // open: cin, cout
  Adder #(.width(5)) adder_53 (.a(5'b00100), .b(5'b11000), .out(adder_53_out));  // open: cin, cout
  Adder #(.width(5)) adder_54 (.a(5'b00101), .b(5'b11000), .out(adder_54_out));  // open: cin, cout
  Adder #(.width(5)) adder_55 (.a(5'b00110), .b(5'b11000), .out(adder_55_out));  // open: cin, cout
  Adder #(.width(5)) adder_56 (.a(5'b00111), .b(5'b11000), .out(adder_56_out));  // open: cin, cout
  Adder #(.width(5)) adder_57 (.a({5{1'b0}}), .b(5'b11000), .out(adder_57_out));  // open: cin, cout
  Adder #(.width(5)) adder_58 (.a(5'b00001), .b(5'b11000), .out(adder_58_out));  // open: cin, cout
  Adder #(.width(5)) adder_59 (.a(5'b00010), .b(5'b11000), .out(adder_59_out));  // open: cin, cout
  Adder #(.width(5)) adder_60 (.a(5'b00011), .b(5'b11000), .out(adder_60_out));  // open: cin, cout
  Adder #(.width(5)) adder_61 (.a(5'b00100), .b(5'b11000), .out(adder_61_out));  // open: cin, cout
  Adder #(.width(5)) adder_62 (.a(5'b00101), .b(5'b11000), .out(adder_62_out));  // open: cin, cout
  Adder #(.width(5)) adder_63 (.a(5'b00110), .b(5'b11000), .out(adder_63_out));  // open: cin, cout
  Adder #(.width(5)) adder_64 (.a(5'b00111), .b(5'b11000), .out(adder_64_out));  // open: cin, cout
  Multiplexer #(.width(32)) multiplexer_49 (
    .in0({32{1'b0}}), .in1(r24), .out(multiplexer_49_out), .sel(comparator_80_eq));
  Comparator #(.width(5)) comparator_80 (.a(ReadIndex1), .b(adder_49_out), .eq(comparator_80_eq));  // open: gt, lt
  Multiplexer #(.width(32)) multiplexer_50 (
    .in0({32{1'b0}}), .in1(r25), .out(multiplexer_50_out), .sel(comparator_81_eq));
  Comparator #(.width(5)) comparator_81 (.a(ReadIndex1), .b(adder_50_out), .eq(comparator_81_eq));  // open: gt, lt
  Multiplexer #(.width(32)) multiplexer_51 (
    .in0({32{1'b0}}), .in1(r26), .out(multiplexer_51_out), .sel(comparator_82_eq));
  Comparator #(.width(5)) comparator_82 (.a(ReadIndex1), .b(adder_51_out), .eq(comparator_82_eq));  // open: gt, lt
  Multiplexer #(.width(32)) multiplexer_52 (
    .in0({32{1'b0}}), .in1(r27), .out(multiplexer_52_out), .sel(comparator_83_eq));
  Comparator #(.width(5)) comparator_83 (.a(ReadIndex1), .b(adder_52_out), .eq(comparator_83_eq));  // open: gt, lt
  Multiplexer #(.width(32)) multiplexer_53 (
    .in0({32{1'b0}}), .in1(r28), .out(multiplexer_53_out), .sel(comparator_84_eq));
  Comparator #(.width(5)) comparator_84 (.a(ReadIndex1), .b(adder_53_out), .eq(comparator_84_eq));  // open: gt, lt
  Multiplexer #(.width(32)) multiplexer_54 (
    .in0({32{1'b0}}), .in1(r29), .out(multiplexer_54_out), .sel(comparator_85_eq));
  Comparator #(.width(5)) comparator_85 (.a(ReadIndex1), .b(adder_54_out), .eq(comparator_85_eq));  // open: gt, lt
  Multiplexer #(.width(32)) multiplexer_55 (
    .in0({32{1'b0}}), .in1(r30), .out(multiplexer_55_out), .sel(comparator_86_eq));
  Comparator #(.width(5)) comparator_86 (.a(ReadIndex1), .b(adder_55_out), .eq(comparator_86_eq));  // open: gt, lt
  Multiplexer #(.width(32)) multiplexer_56 (
    .in0({32{1'b0}}), .in1(r31), .out(multiplexer_56_out), .sel(comparator_87_eq));
  Comparator #(.width(5)) comparator_87 (.a(ReadIndex1), .b(adder_56_out), .eq(comparator_87_eq));  // open: gt, lt
  Comparator #(.width(5)) comparator_88 (.a(ReadIndex2), .b(adder_57_out), .eq(comparator_88_eq));  // open: gt, lt
  Comparator #(.width(5)) comparator_89 (.a(ReadIndex2), .b(adder_58_out), .eq(comparator_89_eq));  // open: gt, lt
  Comparator #(.width(5)) comparator_90 (.a(ReadIndex2), .b(adder_59_out), .eq(comparator_90_eq));  // open: gt, lt
  Comparator #(.width(5)) comparator_91 (.a(ReadIndex2), .b(adder_60_out), .eq(comparator_91_eq));  // open: gt, lt
  Comparator #(.width(5)) comparator_92 (.a(ReadIndex2), .b(adder_61_out), .eq(comparator_92_eq));  // open: gt, lt
  Comparator #(.width(5)) comparator_93 (.a(ReadIndex2), .b(adder_62_out), .eq(comparator_93_eq));  // open: gt, lt
  Comparator #(.width(5)) comparator_94 (.a(ReadIndex2), .b(adder_63_out), .eq(comparator_94_eq));  // open: gt, lt
  Comparator #(.width(5)) comparator_95 (.a(ReadIndex2), .b(adder_64_out), .eq(comparator_95_eq));  // open: gt, lt
  Multiplexer #(.width(32)) multiplexer_57 (
    .in0({32{1'b0}}), .in1(r24), .out(multiplexer_57_out), .sel(comparator_88_eq));
  Multiplexer #(.width(32)) multiplexer_58 (
    .in0({32{1'b0}}), .in1(r25), .out(multiplexer_58_out), .sel(comparator_89_eq));
  Multiplexer #(.width(32)) multiplexer_59 (
    .in0({32{1'b0}}), .in1(r26), .out(multiplexer_59_out), .sel(comparator_90_eq));
  Multiplexer #(.width(32)) multiplexer_60 (
    .in0({32{1'b0}}), .in1(r27), .out(multiplexer_60_out), .sel(comparator_91_eq));
  Multiplexer #(.width(32)) multiplexer_61 (
    .in0({32{1'b0}}), .in1(r28), .out(multiplexer_61_out), .sel(comparator_92_eq));
  Multiplexer #(.width(32)) multiplexer_62 (
    .in0({32{1'b0}}), .in1(r29), .out(multiplexer_62_out), .sel(comparator_93_eq));
  Multiplexer #(.width(32)) multiplexer_63 (
    .in0({32{1'b0}}), .in1(r30), .out(multiplexer_63_out), .sel(comparator_94_eq));
  Multiplexer #(.width(32)) multiplexer_64 (
    .in0({32{1'b0}}), .in1(r31), .out(multiplexer_64_out), .sel(comparator_95_eq));
  assign or_9_out = multiplexer_49_out | multiplexer_50_out | multiplexer_51_out | multiplexer_52_out | multiplexer_53_out | multiplexer_54_out | multiplexer_55_out | multiplexer_56_out;  // OR_Gate or_9, 32 bits wide
  assign or_10_out = multiplexer_57_out | multiplexer_58_out | multiplexer_59_out | multiplexer_60_out | multiplexer_61_out | multiplexer_62_out | multiplexer_63_out | multiplexer_64_out;  // OR_Gate or_10, 32 bits wide

  // Other names for the same wires on the sheet: r1[31:0] = ra; r2[31:0] = sp; r5[31:0] = t0; r6[31:0] = t1;
  //   r7[31:0] = t2; r8[31:0] = s0; r9[31:0] = s1; r10[31:0] = a0

  // Notes on the sheet:
  //   INPUTS to your circuit
  //   DON'T CHANGE THE LOCATIONS OF THE INPUTS AND OUTPUTS!
  //   These are DEBUG/TEST outputs from your circuit.
  //   OUTPUTS from your circuit
endmodule
